# Fritzing sketch sparkcopter-shield (saved by Fritzing 0.9.2b)
circuit board: 2.06939cm x 3.76715cm
breadboards: 1

parts:
  M1 = Molex PicoBlade Header 2-pin [part_number=53047-0410]
  M2 = Molex PicoBlade Header 2-pin [part_number=53047-0410]
  M3 = Molex PicoBlade Header 2-pin [part_number=53047-0410]
  M4 = Molex PicoBlade Header 2-pin [part_number=53047-0410]
  Q1 = MOSFET-NCHANNEL [package=sot23-3]
  Q2 = MOSFET-NCHANNEL [package=sot23-3]
  Q3 = MOSFET-NCHANNEL [package=sot23-3]
  Q4 = MOSFET-NCHANNEL [package=sot23-3]
  -_+ = Battery
  Spark_Core_Socket = Spark Core Socket
  CMCJU_10DOF = CJMCU - 10DOF
  C1 = Capacitor [package=cap-pth-small]

nets:
  N1: M1.1, Q1.D
  N2: M1.2, M2.2, M3.2, M4.2, -_+.+, Spark_Core_Socket.VIN, C1.1
  N3: M2.1, Q2.D
  N4: M3.1, Q3.D
  N5: M4.1, Q4.D
  N6: Q1.G, Spark_Core_Socket.A0
  GND: Q1.S, Q2.S, Q3.S, Q4.S, -_+.-, Spark_Core_Socket.GND, CMCJU_10DOF.GND, C1.2
  N7: Q2.G, Spark_Core_Socket.A1
  N8: Q3.G, Spark_Core_Socket.A4
  N9: Q4.G, Spark_Core_Socket.A5
  N10: Spark_Core_Socket.D0, CMCJU_10DOF.SDA
  N11: Spark_Core_Socket.D1, CMCJU_10DOF.SCL
  3V3: Spark_Core_Socket.3V3, CMCJU_10DOF.3V3

notes:
  ⬆
  Sparkcopter
  v0.2

custom parts:
  Molex PicoBlade Header 2-pin: 1.25mm Pitch PicoBlade Header Vertical
  Spark Core Socket: 24-pin header for Spark Core and Photon
  CJMCU - 10DOF: CJMCU 10DOF 9-Axis MPU9250+BMP180 Gyro Acceleration Barometer Sensor Module
